// Logisim project proyecto.circ as structural Verilog: 1 circuit, main circuit main
module main (
  input  A,
  input  B,
  input  C,
  input  D,
  input  E,
  input  _257,
  input  _258,
  input  _259,
  input  _261,
  input  _262,
  input  in_11,
  output [3:0] out_12,
  output [3:0] out_13,
  output [2:0] out_14
);

  wire and_1_out, and_2_out, clock_1_out, multiplexer_1_out, not_1_out;
  wire [5:0] counter_1_q;

  or or_1 (out_13[3], A, B, C, D, E, and_1_out);
  and and_1 (and_1_out, not_1_out, and_2_out);
  or or_2 (out_13[2], E, out_14[2]);
  and and_2 (and_2_out, out_14[2], out_13[1]);
  ROM #(.addrWidth(4), .dataWidth(4)) rom_1 (.addr(out_13), .data(out_12));
  Multiplexer #(.select(3)) multiplexer_1 (
    .in0(_257), .in1(_258), .in2(_259), .in3(_261), .in4(_262), .in5(in_11), .out(multiplexer_1_out),
    .sel({out_14[2], out_13[1:0]}));  // open: in6, in7
  Clock clock_1 (.out(clock_1_out));
  not not_1 (not_1_out, out_13[0]);
  Counter #(.max('h1ff), .width(9)) counter_1 (
    .load(out_13[3]), .up(1'b1), .count(multiplexer_1_out), .clk(clock_1_out), .D({6'b100000, out_12[2:0]}),
    .Q({counter_1_q, out_14[2], out_13[1:0]}));  // open: clr, carry

  assign out_14[1:0] = out_13[1:0];

  // Notes on the sheet:
  //   260
  //   contents of rom_1 (hex, n*v repeats v):
  //   8*0 3 0 4 3 0 0 0 5
endmodule
